// Logisim project 5-Stage-Pipeline-MAIN_TEST.circ as structural Verilog: 1 circuit, main circuit main
module main (
);

  wire ALU_Control_p6, ALU_p4, and_1_out, and_2_out, button_1_out, clock_1_out, comparator_1_eq,
       Control_Unit_alusrc, Control_Unit_branch, Control_Unit_halt, Control_Unit_immsrc,
       Control_Unit_memread, Control_Unit_memtoreg, Control_Unit_memwrite, Control_Unit_put,
       Control_Unit_regdst, Control_Unit_regwrite, EX_MEM_Control_halt_2, EX_MEM_Control_memtoreg_2,
       EX_MEM_Control_regwrite_2, FLUSH_q, ID_EX_Control_halt_2, ID_EX_Control_memread_2,
       ID_EX_Control_memtoreg_2, ID_EX_Control_memwrite_2, ID_EX_Control_put_2, ID_EX_Control_regdst_2,
       ID_EX_Control_regwrite_2, ID_EX_Main_Latch_p3, ID_EX_Main_Latch_p7, ID_EX_Main_Latch_p8,
       Instruction_Splitter_p3, Instruction_Splitter_p4, Instruction_Splitter_p5, Instruction_Splitter_p6,
       Instruction_Splitter_p7, MEM_WB_Control_halt_2, MEM_WB_Control_memtoreg_2, MRM_WB_Main_Latch_p6,
       not_1_out, Registers_p4, Sign_Extender__Imm_Gen_p3;
  wire [1:0] undriven, undriven_2;
  wire [3:0] Instruction_Splitter_p2;
  wire [7:0] adder_1_out, adder_2_out, alutoram_1_p2, Instruction_Splitter_p8, multiplexer_2_out, PC_q,
       PC_REG_q;
  wire [15:0] EX_MEM_Main_Latch_p4, EX_MEM_Main_Latch_p5, ID_EX_Main_Latch_p4, ID_EX_Main_Latch_p5,
       ID_EX_Main_Latch_p6, IF_ID_q, MRM_WB_Main_Latch_p3, MRM_WB_Main_Latch_p4, MRM_WB_Main_Latch_p5,
       multiplexer_3_out, multiplexer_4_out, multiplexer_5_out, ram_1_data, register_1_q, Registers_p3,
       Registers_p6, Registers_p7, rom_1_data;

  Multiplexer multiplexer_1 ();  // open: in0, in1, out, sel, en
  Clock clock_1 (.out(clock_1_out));
  Multiplexer #(.width(8), .enable("false")) multiplexer_2 (
    .in0(adder_1_out), .in1(adder_2_out), .out(multiplexer_2_out), .sel(and_2_out));
  not not_1 (not_1_out, ID_EX_Control_halt_2);
  Register PC (.D(multiplexer_2_out), .en(and_1_out), .Q(PC_q), .clk(clock_1_out), .clr(button_1_out));
  Button button_1 (.out(button_1_out));
  and and_1 (and_1_out, not_1_out, 1'b1);
  Adder adder_1 (.a(PC_q), .b(8'h1), .out(adder_1_out));  // open: cin, cout
  ROM #(.dataWidth(16)) rom_1 (.addr(PC_q), .data(rom_1_data), .sel(1'b1));
  Register #(.width(16)) IF_ID (.D(rom_1_data), .Q(IF_ID_q), .clk(clock_1_out));  // open: en, clr
  Register PC_REG (.D(PC_q), .Q(PC_REG_q), .clk(clock_1_out));  // open: en, clr
  // InstructionSplitter Instruction_Splitter: pin names not known; wires that end beside it: IF_ID_q, Instruction_Splitter_p2, Instruction_Splitter_p3, Instruction_Splitter_p4, Instruction_Splitter_p5, Instruction_Splitter_p6, Instruction_Splitter_p7, Instruction_Splitter_p8
  // Decoder_2_ALU ALU_Control: pin names not known; wires that end beside it: Instruction_Splitter_p2[3], Instruction_Splitter_p2[2], Instruction_Splitter_p2[1], Instruction_Splitter_p2[0], Instruction_Splitter_p6, ALU_Control_p6
  Decoder_1 Control_Unit (
    .Opcode3(Instruction_Splitter_p2[3]), .Opcode2(Instruction_Splitter_p2[2]),
    .Opcode1(Instruction_Splitter_p2[1]), .Opcode0(Instruction_Splitter_p2[0]),
    .Subop(Instruction_Splitter_p6), .Unisigned(Instruction_Splitter_p7), .RegWrite(Control_Unit_regwrite),
    .RegDst(Control_Unit_regdst), .ALUSrc(Control_Unit_alusrc), .MemRead(Control_Unit_memread),
    .MemWrite(Control_Unit_memwrite), .MemToReg(Control_Unit_memtoreg), .Branch(Control_Unit_branch),
    .Halt(Control_Unit_halt), .Put(Control_Unit_put), .ImmSrc(Control_Unit_immsrc));
  // RegisterFile Registers: pin names not known; wires that end beside it: Instruction_Splitter_p3, Instruction_Splitter_p4, Registers_p3, Registers_p4, clock_1_out, Registers_p6, Registers_p7
  and and_2 (and_2_out, comparator_1_eq, Control_Unit_branch);
  // SignExtend Sign_Extender__Imm_Gen: pin names not known; wires that end beside it: Instruction_Splitter_p7, Instruction_Splitter_p8, Sign_Extender__Imm_Gen_p3, Sign_Extender__Imm_Gen_p3, Instruction_Splitter_p5, ALU_Control_p6
  Comparator #(.width(16)) comparator_1 (.a(Registers_p6), .b(Registers_p7), .eq(comparator_1_eq));  // open: gt, lt
  Adder adder_2 (.a(Instruction_Splitter_p8), .b(PC_REG_q), .out(adder_2_out));  // open: cin, cout
  Control_Latch ID_EX_Control (
    .RegWrite(Control_Unit_regwrite), .RegDst(Control_Unit_regdst), .ALUSrc(Control_Unit_alusrc),
    .MemRead(Control_Unit_memread), .MemWrite(Control_Unit_memwrite), .MemToReg(Control_Unit_memtoreg),
    .Branch(Control_Unit_branch), .Halt(Control_Unit_halt), .Put(Control_Unit_put),
    .ImmSrc(Control_Unit_immsrc), .RegWrite_2(ID_EX_Control_regwrite_2), .RegDst_2(ID_EX_Control_regdst_2),
    .MemRead_2(ID_EX_Control_memread_2), .MemWrite_2(ID_EX_Control_memwrite_2),
    .MemToReg_2(ID_EX_Control_memtoreg_2), .Halt_2(ID_EX_Control_halt_2), .Put_2(ID_EX_Control_put_2),
    .Enable(ID_EX_Main_Latch_p3), .Clock(clock_1_out));  // open: ALUSrc_2, Branch_2, ImmSrc_2
  // ID_EX_Main_Latch ID_EX_Main_Latch: pin names not known; wires that end beside it: Registers_p6, Registers_p7, ID_EX_Main_Latch_p3, ID_EX_Main_Latch_p4, ID_EX_Main_Latch_p5, ID_EX_Main_Latch_p6, ID_EX_Main_Latch_p7, ID_EX_Main_Latch_p8
  Multiplexer #(.select(2), .width(16), .enable("false")) multiplexer_3 (
    .in1(ID_EX_Main_Latch_p4), .in2(EX_MEM_Main_Latch_p4), .in3(MRM_WB_Main_Latch_p3),
    .out(multiplexer_3_out), .sel(undriven));  // open: in0
  Multiplexer #(.select(2), .width(16), .enable("false")) multiplexer_4 (
    .in1(ID_EX_Main_Latch_p5), .in2(EX_MEM_Main_Latch_p4), .in3(MRM_WB_Main_Latch_p3),
    .out(multiplexer_4_out), .sel(undriven_2));  // open: in0
  Multiplexer #(.width(16), .enable("false")) multiplexer_5 (
    .in0(multiplexer_4_out), .in1(ID_EX_Main_Latch_p6), .out(multiplexer_5_out));  // open: sel
  Register #(.width(16)) register_1 (
    .D(ID_EX_Main_Latch_p4), .en(ID_EX_Control_put_2), .Q(register_1_q), .clk(clock_1_out));  // open: clr
  // sixteen_bit_ALU ALU: pin names not known; wires that end beside it: ID_EX_Main_Latch_p8, multiplexer_3_out, multiplexer_5_out, ALU_p4
  Hex_Digit_Display hex_digit_display_1 (.value(register_1_q[15:12]));  // open: dp
  Hex_Digit_Display hex_digit_display_2 (.value(register_1_q[11:8]));  // open: dp
  Hex_Digit_Display hex_digit_display_3 (.value(register_1_q[7:4]));  // open: dp
  Hex_Digit_Display hex_digit_display_4 (.value(register_1_q[3:0]));  // open: dp
  // EX_MEM_Main_Latch EX_MEM_Main_Latch: pin names not known; wires that end beside it: ALU_p4, ID_EX_Main_Latch_p5, ID_EX_Main_Latch_p7, EX_MEM_Main_Latch_p4, EX_MEM_Main_Latch_p5
  Control_Latch EX_MEM_Control (
    .RegWrite(ID_EX_Control_regwrite_2), .RegDst(ID_EX_Control_regdst_2), .MemRead(ID_EX_Control_memread_2),
    .MemWrite(ID_EX_Control_memwrite_2), .MemToReg(ID_EX_Control_memtoreg_2), .Halt(ID_EX_Control_halt_2),
    .RegWrite_2(EX_MEM_Control_regwrite_2), .MemToReg_2(EX_MEM_Control_memtoreg_2),
    .Halt_2(EX_MEM_Control_halt_2), .Clock(clock_1_out));  // open: ALUSrc, Branch, Put, ImmSrc, RegDst_2, ALUSrc_2, MemRead_2, MemWrite_2, Branch_2, Put_2, ImmSrc_2, Enable
  // ALUtoRAM alutoram_1: pin names not known; wires that end beside it: EX_MEM_Main_Latch_p4, alutoram_1_p2
  RAM #(.dataWidth(16), .bus("separate")) ram_1 (
    .addr(alutoram_1_p2), .din(EX_MEM_Main_Latch_p5), .data(ram_1_data), .clk(clock_1_out));  // open: str, sel, ld, clr
  Control_Latch MEM_WB_Control (
    .RegWrite(EX_MEM_Control_regwrite_2), .MemToReg(EX_MEM_Control_memtoreg_2), .Halt(EX_MEM_Control_halt_2),
    .RegWrite_2(Registers_p4), .MemToReg_2(MEM_WB_Control_memtoreg_2), .Halt_2(MEM_WB_Control_halt_2),
    .Clock(clock_1_out));  // open: RegDst, ALUSrc, MemRead, MemWrite, Branch, Put, ImmSrc, RegDst_2, ALUSrc_2, MemRead_2, MemWrite_2, Branch_2, Put_2, ImmSrc_2, Enable
  // MEM_WB_Latch MRM_WB_Main_Latch: pin names not known; wires that end beside it: ram_1_data, EX_MEM_Main_Latch_p4, MRM_WB_Main_Latch_p3, MRM_WB_Main_Latch_p4, MRM_WB_Main_Latch_p5, MRM_WB_Main_Latch_p6
  Multiplexer #(.width(16), .enable("false")) multiplexer_6 (
    .in0(MRM_WB_Main_Latch_p4), .in1(MRM_WB_Main_Latch_p5), .out(Registers_p3),
    .sel(MEM_WB_Control_memtoreg_2));
  Register #(.width(1)) FLUSH (.D(MEM_WB_Control_halt_2), .Q(FLUSH_q), .clk(clock_1_out));  // open: en, clr
  LED Halt ();  // open: in
  Multiplexer multiplexer_7 ();  // open: in0, in1, out, sel, en

  // Notes on the sheet:
  //   CONNECT ENABLES!!!
  //   FULL BOARD RESET NECESSARY?
  //   IF
  //   IS DECODER CORRECT?
  //   ID
  //   EX
  //   OTHER ALU OUTPUTS?
  //   Forwarding Unit #BITS WRONG
  //   CORRECT ADRESS SETUP?
  //   TO WB WRITE DATA
  //   MEM
  //   WRITE REG
  //   WB
endmodule
